# Fritzing sketch Auto-Repeat Button (saved by Fritzing 0.6.3b)
breadboards: 1

parts:
  Netduino1 = Netduino
  S1 = Pushbutton [package="[THT]"]

nets:
  N1: Netduino1.GND, S1.Pin_3, S1.Pin_4
  N2: S1.Pin_1, S1.Pin_2
