# Fritzing sketch Matrix KeyPad (saved by Fritzing 0.6.3b)

parts:
  Netduino1 = Netduino
  Matrix_Keypad = female pin header, 7 pins [form="♀ (female)"]

nets:
  N1: Netduino1.D7_RTS1, Matrix_Keypad.pin1
  N2: Netduino1.D6_PWM1, Matrix_Keypad.pin2
  N3: Netduino1.D5_PWM0, Matrix_Keypad.pin3
  N4: Netduino1.D4_CS0, Matrix_Keypad.pin4
  N5: Netduino1.D3_TX1, Matrix_Keypad.pin5
  N6: Netduino1.D2_RX1, Matrix_Keypad.pin6
  N7: Netduino1.D1_TX0, Matrix_Keypad.pin7

notes:
  Keep in mind, there are a lot of different matrix keypads, so it's quite possible you need to realign the pins!
