# Fritzing sketch Sharp GP2Y0A02YK Proximity Sensor (saved by Fritzing 0.6.3b)

parts:
  Netduino1 = Netduino
  Proximity_Sensor = female pin header, 3 pins [form="♀ (female)" part_number="Sharp GP2Y0A02YK Proximity Sensor"]

nets:
  N1: Netduino1.+5V, Proximity_Sensor.pin3
  N2: Netduino1.GND, Proximity_Sensor.pin2
  N3: Netduino1.A0, Proximity_Sensor.pin1
