# Fritzing sketch Thumb joystick (saved by Fritzing 0.6.3b)

parts:
  Onderdeel1 = Thumb Joystick
  Netduino1 = Netduino

nets:
  GND: Onderdeel1.GND, Netduino1.GND
  N1: Onderdeel1.SEL, Netduino1.D2_RX1
  N2: Onderdeel1.HORZ, Netduino1.A0
  N3: Onderdeel1.VERT, Netduino1.A1
  VCC: Onderdeel1.VCC, Netduino1.3V3
