# Fritzing sketch RGB Led (saved by Fritzing 0.6.3b)
breadboards: 1

parts:
  Netduino1 = Netduino
  LED1 = RGB LED - (4 legs) [package="5 mm [THT]"]
  R1 = Resistor [tolerance=±5% resistance=220 package=THT]
  R2 = Resistor [tolerance=±5% resistance=220 package=THT]
  R3 = Resistor [tolerance=±5% resistance=220 package=THT]

nets:
  N1: Netduino1.GND, LED1.common_anode
  N2: Netduino1.D9_PWM2, R1.Pin_1
  N3: Netduino1.D6_PWM1, R2.Pin_1
  N4: Netduino1.D5_PWM0, R3.Pin_1
  N5: LED1.red_cathode, R1.Pin_0
  N6: LED1.green_cathode, R2.Pin_0
  N7: LED1.blue_cathode, R3.Pin_0

notes:
  This schematic is for common cathode leds.
  When the led is common anode, the black wire should go to +3.3v instead of Gnd
