# Fritzing sketch SN754410 Motor Driver (saved by Fritzing 0.6.3b)
breadboards: 1

parts:
  Netduino1 = Netduino
  IC1 = IC, DIP package, 16 pins [chip_label=SN754410 spacing=300mil]
  M2 = DC Motor
  M3 = DC Motor

nets:
  N1: Netduino1.D7_RTS1, IC1.pin2
  N2: Netduino1.D6_PWM1, IC1.pin7
  N3: Netduino1.D5_PWM0, IC1.pin15
  N4: Netduino1.D4_CS0, IC1.pin10
  N5: Netduino1.+5V, IC1.pin1, IC1.pin9, IC1.pin16
  N6: Netduino1.GND, IC1.pin4, IC1.pin5, IC1.pin12, IC1.pin13
  N7: Netduino1.VIN, IC1.pin8
  N8: IC1.pin3, M3.pin_2
  N9: IC1.pin6, M3.pin_1
  N10: IC1.pin11, M2.pin_2
  N11: IC1.pin14, M2.pin_1
