# Fritzing sketch Wearable Keypad (saved by Fritzing 0.6.3b)

parts:
  Netduino1 = Netduino
  Wearable_Keypad = female pin header, 6 pins [form="♂ (male)"]

nets:
  N1: Netduino1.GND, Wearable_Keypad.pin3
  N2: Netduino1.D7_RTS1, Wearable_Keypad.pin6
  N3: Netduino1.D6_PWM1, Wearable_Keypad.pin5
  N4: Netduino1.D5_PWM0, Wearable_Keypad.pin4
  N5: Netduino1.3V3, Wearable_Keypad.pin2
