# Fritzing sketch InfraredTx (saved by Fritzing 0.8.5b)
breadboards: 1

parts:
  Part1 = Max Power IR LED Kit
  Part2 = Arduino BT
  R1 = Resistor [tolerance=±5% resistance=33 package=THT]

nets:
  N1: Part1.GND, Part2.MOSI/PWM_D11
  N2: Part1.VCC, R1.Pin_1
